# Fritzing sketch ledCube (saved by Fritzing 0.9.3b)
perfboards: 1

parts:
  부품1 = Arduino Mega 2560 (Rev3)
  J1 = Piezo Speaker
  LCD1 = LCD screen
  R5 = Resistor [tolerance=±5% resistance=220 package=THT]
  R6 = Resistor [tolerance=±5% resistance=220 package=THT]
  R7 = Rotary Potentiometer (Small) [maximum_resistance=100kΩ package=THT]
  S1 = Pushbutton [package="[THT]"]
  S2 = Toggle Switch [package=THT]
  LED135 = LED - 5mm [color="Red (633nm)" package="5 mm [THT]"]
  LED140 = LED - 5mm [color="Red (633nm)" package="5 mm [THT]"]  # not connected
  LED145 = LED - 5mm [color="Red (633nm)" package="5 mm [THT]"]  # not connected
  LED148 = LED - 5mm [color="Red (633nm)" package="5 mm [THT]"]  # not connected
  LED150 = LED - 5mm [color="Red (633nm)" package="5 mm [THT]"]  # not connected
  R8 = Resistor [tolerance=±5% resistance=220 package=THT]  # not connected
  LED178 = LED - 5mm [color="Red (633nm)" package="5 mm [THT]"]  # not connected
  LED183 = LED - 5mm [color="Red (633nm)" package="5 mm [THT]"]
  LED188 = LED - 5mm [color="Red (633nm)" package="5 mm [THT]"]  # not connected
  LED193 = LED - 5mm [color="Red (633nm)" package="5 mm [THT]"]
  LED198 = LED - 5mm [color="Red (633nm)" package="5 mm [THT]"]  # not connected
  LED206 = LED - 5mm [color="Red (633nm)" package="5 mm [THT]"]
  LED208 = LED - 5mm [color="Red (633nm)" package="5 mm [THT]"]  # not connected
  LED216 = LED - 5mm [color="Red (633nm)" package="5 mm [THT]"]  # not connected
  LED220 = LED - 5mm [color="Red (633nm)" package="5 mm [THT]"]  # not connected
  LED224 = LED - 5mm [color="Red (633nm)" package="5 mm [THT]"]  # not connected
  R10 = Resistor [tolerance=±5% resistance=220 package=THT]
  LED338 = LED - 5mm [color="Red (633nm)" package="5 mm [THT]"]  # not connected
  LED343 = LED - 5mm [color="Red (633nm)" package="5 mm [THT]"]
  LED348 = LED - 5mm [color="Red (633nm)" package="5 mm [THT]"]  # not connected
  LED353 = LED - 5mm [color="Red (633nm)" package="5 mm [THT]"]
  LED358 = LED - 5mm [color="Red (633nm)" package="5 mm [THT]"]  # not connected
  LED363 = LED - 5mm [color="Red (633nm)" package="5 mm [THT]"]  # not connected
  LED368 = LED - 5mm [color="Red (633nm)" package="5 mm [THT]"]
  LED373 = LED - 5mm [color="Red (633nm)" package="5 mm [THT]"]  # not connected
  LED378 = LED - 5mm [color="Red (633nm)" package="5 mm [THT]"]  # not connected
  LED383 = LED - 5mm [color="Red (633nm)" package="5 mm [THT]"]  # not connected
  LED384 = LED - 5mm [color="Red (633nm)" package="5 mm [THT]"]  # not connected
  LED385 = LED - 5mm [color="Red (633nm)" package="5 mm [THT]"]  # not connected
  LED386 = LED - 5mm [color="Red (633nm)" package="5 mm [THT]"]  # not connected
  LED387 = LED - 5mm [color="Red (633nm)" package="5 mm [THT]"]  # not connected
  LED388 = LED - 5mm [color="Red (633nm)" package="5 mm [THT]"]  # not connected
  LED389 = LED - 5mm [color="Red (633nm)" package="5 mm [THT]"]  # not connected
  LED390 = LED - 5mm [color="Red (633nm)" package="5 mm [THT]"]  # not connected
  LED391 = LED - 5mm [color="Red (633nm)" package="5 mm [THT]"]  # not connected
  LED392 = LED - 5mm [color="Red (633nm)" package="5 mm [THT]"]  # not connected
  LED393 = LED - 5mm [color="Red (633nm)" package="5 mm [THT]"]  # not connected
  LED394 = LED - 5mm [color="Red (633nm)" package="5 mm [THT]"]  # not connected
  LED395 = LED - 5mm [color="Red (633nm)" package="5 mm [THT]"]  # not connected
  LED396 = LED - 5mm [color="Red (633nm)" package="5 mm [THT]"]  # not connected
  LED397 = LED - 5mm [color="Red (633nm)" package="5 mm [THT]"]  # not connected
  LED398 = LED - 5mm [color="Red (633nm)" package="5 mm [THT]"]  # not connected
  LED399 = LED - 5mm [color="Red (633nm)" package="5 mm [THT]"]  # not connected
  LED400 = LED - 5mm [color="Red (633nm)" package="5 mm [THT]"]  # not connected
  LED401 = LED - 5mm [color="Red (633nm)" package="5 mm [THT]"]  # not connected
  LED402 = LED - 5mm [color="Red (633nm)" package="5 mm [THT]"]  # not connected
  LED403 = LED - 5mm [color="Red (633nm)" package="5 mm [THT]"]  # not connected
  LED404 = LED - 5mm [color="Red (633nm)" package="5 mm [THT]"]  # not connected
  LED405 = LED - 5mm [color="Red (633nm)" package="5 mm [THT]"]  # not connected
  LED406 = LED - 5mm [color="Red (633nm)" package="5 mm [THT]"]  # not connected
  LED407 = LED - 5mm [color="Red (633nm)" package="5 mm [THT]"]  # not connected
  LED408 = LED - 5mm [color="Red (633nm)" package="5 mm [THT]"]  # not connected
  LED409 = LED - 5mm [color="Red (633nm)" package="5 mm [THT]"]  # not connected
  LED410 = LED - 5mm [color="Red (633nm)" package="5 mm [THT]"]  # not connected
  LED411 = LED - 5mm [color="Red (633nm)" package="5 mm [THT]"]  # not connected
  LED412 = LED - 5mm [color="Red (633nm)" package="5 mm [THT]"]  # not connected
  LED413 = LED - 5mm [color="Red (633nm)" package="5 mm [THT]"]  # not connected
  LED414 = LED - 5mm [color="Red (633nm)" package="5 mm [THT]"]  # not connected
  LED415 = LED - 5mm [color="Red (633nm)" package="5 mm [THT]"]  # not connected
  LED416 = LED - 5mm [color="Red (633nm)" package="5 mm [THT]"]  # not connected
  LED417 = LED - 5mm [color="Red (633nm)" package="5 mm [THT]"]  # not connected
  LED418 = LED - 5mm [color="Red (633nm)" package="5 mm [THT]"]  # not connected
  LED419 = LED - 5mm [color="Red (633nm)" package="5 mm [THT]"]  # not connected
  LED420 = LED - 5mm [color="Red (633nm)" package="5 mm [THT]"]  # not connected
  LED421 = LED - 5mm [color="Red (633nm)" package="5 mm [THT]"]  # not connected
  LED422 = LED - 5mm [color="Red (633nm)" package="5 mm [THT]"]  # not connected
  LED423 = LED - 5mm [color="Red (633nm)" package="5 mm [THT]"]  # not connected
  LED424 = LED - 5mm [color="Red (633nm)" package="5 mm [THT]"]  # not connected
  LED425 = LED - 5mm [color="Red (633nm)" package="5 mm [THT]"]  # not connected
  LED426 = LED - 5mm [color="Red (633nm)" package="5 mm [THT]"]  # not connected
  LED427 = LED - 5mm [color="Red (633nm)" package="5 mm [THT]"]  # not connected
  LED428 = LED - 5mm [color="Red (633nm)" package="5 mm [THT]"]  # not connected
  LED429 = LED - 5mm [color="Red (633nm)" package="5 mm [THT]"]  # not connected
  LED430 = LED - 5mm [color="Red (633nm)" package="5 mm [THT]"]  # not connected
  LED431 = LED - 5mm [color="Red (633nm)" package="5 mm [THT]"]  # not connected
  LED432 = LED - 5mm [color="Red (633nm)" package="5 mm [THT]"]  # not connected
  LED433 = LED - 5mm [color="Red (633nm)" package="5 mm [THT]"]  # not connected
  LED434 = LED - 5mm [color="Red (633nm)" package="5 mm [THT]"]  # not connected
  LED435 = LED - 5mm [color="Red (633nm)" package="5 mm [THT]"]  # not connected
  LED436 = LED - 5mm [color="Red (633nm)" package="5 mm [THT]"]  # not connected
  LED437 = LED - 5mm [color="Red (633nm)" package="5 mm [THT]"]  # not connected
  LED438 = LED - 5mm [color="Red (633nm)" package="5 mm [THT]"]
  LED439 = LED - 5mm [color="Red (633nm)" package="5 mm [THT]"]
  LED440 = LED - 5mm [color="Red (633nm)" package="5 mm [THT]"]
  LED441 = LED - 5mm [color="Red (633nm)" package="5 mm [THT]"]  # not connected
  LED442 = LED - 5mm [color="Red (633nm)" package="5 mm [THT]"]  # not connected
  LED443 = LED - 5mm [color="Red (633nm)" package="5 mm [THT]"]  # not connected
  LED444 = LED - 5mm [color="Red (633nm)" package="5 mm [THT]"]
  LED445 = LED - 5mm [color="Red (633nm)" package="5 mm [THT]"]  # not connected
  LED446 = LED - 5mm [color="Red (633nm)" package="5 mm [THT]"]  # not connected
  LED447 = LED - 5mm [color="Red (633nm)" package="5 mm [THT]"]  # not connected
  LED448 = LED - 5mm [color="Red (633nm)" package="5 mm [THT]"]  # not connected
  LED449 = LED - 5mm [color="Red (633nm)" package="5 mm [THT]"]  # not connected
  LED450 = LED - 5mm [color="Red (633nm)" package="5 mm [THT]"]  # not connected
  LED451 = LED - 5mm [color="Red (633nm)" package="5 mm [THT]"]  # not connected
  LED452 = LED - 5mm [color="Red (633nm)" package="5 mm [THT]"]  # not connected
  LED453 = LED - 5mm [color="Red (633nm)" package="5 mm [THT]"]  # not connected
  LED454 = LED - 5mm [color="Red (633nm)" package="5 mm [THT]"]  # not connected
  LED455 = LED - 5mm [color="Red (633nm)" package="5 mm [THT]"]  # not connected
  LED456 = LED - 5mm [color="Red (633nm)" package="5 mm [THT]"]  # not connected
  LED457 = LED - 5mm [color="Red (633nm)" package="5 mm [THT]"]  # not connected
  LED458 = LED - 5mm [color="Red (633nm)" package="5 mm [THT]"]  # not connected
  LED459 = LED - 5mm [color="Red (633nm)" package="5 mm [THT]"]  # not connected
  LED460 = LED - 5mm [color="Red (633nm)" package="5 mm [THT]"]  # not connected
  LED461 = LED - 5mm [color="Red (633nm)" package="5 mm [THT]"]  # not connected
  LED462 = LED - 5mm [color="Red (633nm)" package="5 mm [THT]"]  # not connected
  LED463 = LED - 5mm [color="Red (633nm)" package="5 mm [THT]"]  # not connected
  LED464 = LED - 5mm [color="Red (633nm)" package="5 mm [THT]"]  # not connected
  LED465 = LED - 5mm [color="Red (633nm)" package="5 mm [THT]"]  # not connected
  LED466 = LED - 5mm [color="Red (633nm)" package="5 mm [THT]"]  # not connected
  LED467 = LED - 5mm [color="Red (633nm)" package="5 mm [THT]"]  # not connected
  LED468 = LED - 5mm [color="Red (633nm)" package="5 mm [THT]"]  # not connected
  LED469 = LED - 5mm [color="Red (633nm)" package="5 mm [THT]"]  # not connected
  LED470 = LED - 5mm [color="Red (633nm)" package="5 mm [THT]"]  # not connected
  LED471 = LED - 5mm [color="Red (633nm)" package="5 mm [THT]"]  # not connected
  LED472 = LED - 5mm [color="Red (633nm)" package="5 mm [THT]"]  # not connected
  LED473 = LED - 5mm [color="Red (633nm)" package="5 mm [THT]"]
  LED474 = LED - 5mm [color="Red (633nm)" package="5 mm [THT]"]  # not connected
  LED475 = LED - 5mm [color="Red (633nm)" package="5 mm [THT]"]  # not connected
  LED476 = LED - 5mm [color="Red (633nm)" package="5 mm [THT]"]  # not connected
  LED477 = LED - 5mm [color="Red (633nm)" package="5 mm [THT]"]  # not connected
  LED478 = LED - 5mm [color="Red (633nm)" package="5 mm [THT]"]  # not connected
  LED479 = LED - 5mm [color="Red (633nm)" package="5 mm [THT]"]  # not connected
  LED480 = LED - 5mm [color="Red (633nm)" package="5 mm [THT]"]  # not connected
  LED481 = LED - 5mm [color="Red (633nm)" package="5 mm [THT]"]  # not connected
  LED482 = LED - 5mm [color="Red (633nm)" package="5 mm [THT]"]  # not connected
  LED483 = LED - 5mm [color="Red (633nm)" package="5 mm [THT]"]  # not connected
  R11 = Resistor [tolerance=±5% resistance=220 package=THT]
  R12 = Resistor [tolerance=±5% resistance=220 package=THT]
  R14 = Resistor [tolerance=±5% resistance=220 package=THT]
  R15 = Resistor [tolerance=±5% resistance=220 package=THT]

nets:
  N1: 부품1.A15, R7.wiper
  N2: 부품1.D41, R10.Pin_0
  N3: 부품1.D42, R11.Pin_0
  N4: 부품1.D43, R12.Pin_0
  N5: 부품1.D44, R15.Pin_0
  N6: 부품1.D45, R14.Pin_0
  N7: 부품1.D46, S1.Pin_1, S1.Pin_2
  N8: 부품1.D47, J1.pin2
  N9: 부품1.D48, LCD1.DB7
  N10: 부품1.D49, LCD1.DB6
  N11: 부품1.D50, LCD1.DB5
  N12: 부품1.D51, LCD1.DB4
  N13: 부품1.D52, LCD1.E
  N14: 부품1.D53, LCD1.RS
  N15: J1.pin1, S2.L2
  N16: LCD1.V0, R6.Pin_1
  N17: R5.Pin_1, S2.L1
  N18: LED135.cathode, LED343.cathode
  N19: LED135.anode, LED440.anode
  N20: LED183.cathode, LED353.cathode
  N21: LED193.anode, LED439.anode
  N22: LED206.anode, LED438.anode
  N23: LED343.anode, LED473.anode
  N24: LED368.anode, LED444.anode

notes:
  LCD(53,52,51,50,49,48)
  Buzzer(47)
  Switch(46)
  AR(A16-deltaTime)
  1F
  2F
  3F
  4F
  5F
  (0,0,0)
  (0,5,0)
  (5,0,0)
  (5,5,0)
  pin 6
  pin 5
  pin 4
  pin 3
  pin 2
  pin 45
  pin 44
  pin 43
  pin 42
  pin 41
  pin 40
  pin 36
  pin 38
  pin 39
  pin 37
  pin 35
  pin 33
  pin 32
  pin 34
  pin 31
  pin 28
  pin 29
  pin 27
  pin 30
  pin 26
  pin 7
  pin 22
  pin 24
  pin 25
  pin 23
